// Logisim project Arh_7.circ as structural Verilog: 5 circuits, main circuit 2х канальный мультиплексор
module \_2х_канальный_мультиплексор  (
  input  a,
  input  b,
  input  sel,
  output out
);

  wire not_1_out, \И_2_out , \И_out ;

  not not_1 (not_1_out, sel);
  and \u_И  (\И_out , a, not_1_out);
  and \u_И_2  (\И_2_out , b, sel);
  or \u_ИЛИ  (out, \И_out , \И_2_out );

  // Notes on the sheet:
  //   2х канальный мультиплексор
endmodule

// MUX.
module \_4x_канальный_мультиплексор  (
  input  A0,
  input  A1,
  input  D0,
  input  D1,
  input  D2,
  input  D3,
  output Y
);

  wire not_1_out, not_2_out, \И_2_out , \И_3_out , \И_4_out , \И_out ;

  not not_1 (not_1_out, A0);
  not not_2 (not_2_out, A1);
  and \u_И  (\И_out , not_1_out, not_2_out, D0);
  and \u_И_2  (\И_2_out , not_2_out, A0, D1);
  and \u_И_3  (\И_3_out , not_1_out, D2, A1);
  and \u_И_4  (\И_4_out , A0, D3, A1);
  or \u_ИЛИ  (Y, \И_out , \И_2_out , \И_3_out , \И_4_out );

  // Notes on the sheet:
  //   Адрес
  //   Информационный вход
  //   4х канальный мультиплексор
endmodule

module \_16ти_канальный_мультиплексор  (
  input  D0,
  input  D1,
  input  D2,
  input  D3,
  input  D4,
  input  D5,
  input  D6,
  input  D7,
  input  D8,
  input  D9,
  input  D10,
  input  D11,
  input  D12,
  input  D13,
  input  D14,
  input  D15,
  input  A0,
  input  A1,
  input  A2,
  input  A3,
  output out_21
);

  wire \n4x_канальный_мультиплексор_1_y , \n4x_канальный_мультиплексор_2_y ,
       \n4x_канальный_мультиплексор_3_y , \n4x_канальный_мультиплексор_4_y ;

  \_4x_канальный_мультиплексор  \u_4x_канальный_мультиплексор_1  (
    .A0(A0), .A1(A1), .D0(D0), .D1(D1), .D2(D2), .D3(D3), .Y(\n4x_канальный_мультиплексор_1_y ));
  \_4x_канальный_мультиплексор  \u_4x_канальный_мультиплексор_2  (
    .A0(A0), .A1(A1), .D0(D4), .D1(D5), .D2(D6), .D3(D7), .Y(\n4x_канальный_мультиплексор_2_y ));
  \_4x_канальный_мультиплексор  \u_4x_канальный_мультиплексор_3  (
    .A0(A0), .A1(A1), .D0(D8), .D1(D9), .D2(D10), .D3(D11), .Y(\n4x_канальный_мультиплексор_3_y ));
  \_4x_канальный_мультиплексор  \u_4x_канальный_мультиплексор_4  (
    .A0(A0), .A1(A1), .D0(D12), .D1(D13), .D2(D14), .D3(D15), .Y(\n4x_канальный_мультиплексор_4_y ));
  \_4x_канальный_мультиплексор  \u_4x_канальный_мультиплексор_5  (
    .A0(A2), .A1(A3), .D0(\n4x_канальный_мультиплексор_1_y ), .D1(\n4x_канальный_мультиплексор_2_y ),
    .D2(\n4x_канальный_мультиплексор_3_y ), .D3(\n4x_канальный_мультиплексор_4_y ), .Y(out_21));
  \Демультиплексор  \u_демультиплексор_1  ();  // open: in, sel, a, b

  // Notes on the sheet:
  //   16ти канальный мультиплексор
endmodule

module \Демультиплексор  (
  input  in,
  input  sel,
  output a,
  output b
);

  wire not_1_out;

  not not_1 (not_1_out, sel);
  and \u_И  (a, in, not_1_out);
  and \u_И_2  (b, in, sel);

  // Notes on the sheet:
  //   Демультиплексор
endmodule

module \_16ти_канальный_мультиплексор__стандартные_элементы_Logisim  (
  input  D0,
  input  D1,
  input  D2,
  input  D3,
  input  D4,
  input  D5,
  input  D6,
  input  D7,
  input  D8,
  input  D9,
  input  D10,
  input  D11,
  input  D12,
  input  D13,
  input  D14,
  input  [3:0] sel,
  input  D15,
  output Y
);

  Multiplexer #(.select(4), .enable("false")) multiplexer_1 (
    .in0(D0), .in1(D1), .in2(D2), .in3(D3), .in4(D4), .in5(D5), .in6(D6), .in7(D7), .in8(D8), .in9(D9),
    .in10(D10), .in11(D11), .in12(D12), .in13(D13), .in14(D14), .in15(D15), .out(Y), .sel(sel));

  // Notes on the sheet:
  //   16ти канальный мультиплексор со стандартными элементами 
endmodule
